// Logisim project CN.circ as structural Verilog: 1 circuit, main circuit main
module main (
  input  [1:0] in_1,
  input  [7:0] in_2,
  input  [7:0] in_3,
  input  [1:0] in_4,
  input  in_5,
  input  in_6,
  input  in_7
);

  wire CU_SUB, multiplexer_4_out, not_2_out, NOT_A8, Q0, Q1, Q_1, xor_3_out, xor_4_out;
  wire [1:0] SELECT_M, xor_2_out;
  wire [5:0] SHIFT_Q;
  wire [7:0] M, multiplexer_3_out, multiplexer_6_out;
  wire [8:0] bit_extender_1_out, bit_extender_2_out, BOOTH_RESULT, HOLD_A, multiplexer_1_out,
       multiplexer_2_out, shifter_1_out, shifter_2_out, xor_1_out;

  Multiplexer #(.select(2), .width(9)) multiplexer_1 (
    .in0(HOLD_A), .in1({9{1'b0}}), .in2(shifter_2_out), .in3(BOOTH_RESULT), .out(multiplexer_1_out));  // open: sel
  assign bit_extender_1_out = {{1{M[7]}}, M};  // Bit_Extender bit_extender_1
  Register #(.width(9)) A (.D(multiplexer_1_out), .en(in_7), .clk(in_5), .Q(HOLD_A), .clr(in_6));
  Shifter #(.width(9)) shifter_1 (.in(bit_extender_1_out), .\dist (4'b0001), .out(shifter_1_out));
  assign bit_extender_2_out = {{8{CU_SUB}}, CU_SUB};  // Bit_Extender bit_extender_2
  Multiplexer #(.select(2), .width(9)) multiplexer_2 (
    .in0({9{1'b0}}), .in1(bit_extender_1_out), .in2(shifter_1_out), .in3({9{1'b0}}), .out(multiplexer_2_out),
    .sel(SELECT_M));
  Shifter #(.shift("ar"), .width(9)) shifter_2 (.in(HOLD_A), .\dist (4'b0010), .out(shifter_2_out));
  not not_1 (NOT_A8, HOLD_A[8]);
  assign xor_1_out = bit_extender_2_out ^ multiplexer_2_out;  // XOR_Gate xor_1, 9 bits wide
  Register Q (.D(multiplexer_3_out), .en(in_7), .clk(in_5), .Q({SHIFT_Q, Q1, Q0}), .clr(in_6));
  Multiplexer #(.select(2), .width(8)) multiplexer_3 (
    .in0({SHIFT_Q, Q1, Q0}), .in1(in_2), .in2({HOLD_A[1:0], SHIFT_Q}), .in3({SHIFT_Q, Q1, Q0}),
    .out(multiplexer_3_out));  // open: sel
  Adder #(.width(9)) adder_1 (.a(xor_1_out), .b(HOLD_A), .out(BOOTH_RESULT), .cin(CU_SUB));  // open: cout
  Register #(.width(1)) u_Q_1 (.D(multiplexer_4_out), .en(in_7), .clk(in_5), .Q(Q_1), .clr(in_6));
  Multiplexer #(.select(2)) multiplexer_4 (
    .in0(Q_1), .in1(1'b0), .in2(Q1), .in3(Q_1), .out(multiplexer_4_out));  // open: sel
  xor xor_2 (xor_2_out[0], Q0, Q_1);
  Multiplexer #(.select(2)) multiplexer_5 (.in0(1'b0), .in1(1'b1), .in2(Q1), .in3(NOT_A8), .out(CU_SUB));  // open: sel
  xor xor_3 (xor_3_out, Q1, Q0);
  xor xor_4 (xor_4_out, Q0, Q_1);
  not not_2 (not_2_out, xor_4_out);
  Register u_M (.D(multiplexer_6_out), .en(in_7), .clk(in_5), .Q(M), .clr(in_6));
  Multiplexer #(.select(2), .width(8)) multiplexer_6 (
    .in0(M), .in1(in_3), .in2(M), .in3(M), .out(multiplexer_6_out));  // open: sel
  and and_1 (xor_2_out[1], xor_3_out, not_2_out);
  Multiplexer #(.select(2), .width(2)) multiplexer_7 (
    .in0(2'b01), .in1(2'b01), .in2(xor_2_out), .in3(2'b01), .out(SELECT_M));  // open: sel

  // Other names for the same wires on the sheet: A_IN[7:0] = in_2; B_IN[7:0] = in_3; CLK = in_5; ENABLE = in_7;
  //   OPCODE[1:0] = in_1; REG_A[8:0] = HOLD_A; RST = in_6; SHIFT_Q[7:6] = HOLD_A[1:0]; STATE[1:0] = in_4

  // Notes on the sheet:
  //   2*M(M << 1)
  //   0;M;2M;Don't care
  //   SELECT_M[0]
endmodule
